// Logisim project D_Flip_Flop_Asy_circ.circ as structural Verilog
module main (
  input  in_1,
  input  in_2,
  input  in_3,
  input  in_4,
  output out_5
);

  D_Flip_Flop_Asy d_flip_flop_asy_1 (.clk(in_1), .d(in_2), .set(in_3), .clr(in_4), .q(out_5));
endmodule

// VHDL entity D_Flip_Flop_Asy, as the project stores it:
--------------------------------------------------------------------------------
-- Project :
-- File    :
-- Autor   :
-- Date    :
--
--------------------------------------------------------------------------------
-- Description :
--
--------------------------------------------------------------------------------

LIBRARY ieee;
USE ieee.std_logic_1164.all;

ENTITY D_Flip_Flop_Asy IS
  PORT (
    clk : IN std_logic;
    d   : IN std_logic;
    set : IN std_logic;
    clr : IN std_logic;
    q   : OUT std_logic
    );
END D_Flip_Flop_Asy;

--------------------------------------------------------------------------------
--Complete your VHDL description below
--------------------------------------------------------------------------------

ARCHITECTURE bhv OF D_Flip_Flop_Asy IS

BEGIN
    process(clk, set, clr)
    begin
        if clr = '1' then
            q <= '0';

        elsif set = '1' then
            q <= '1';

        elsif rising_edge(clk) then
            q <= d;
        end if;
    end process;

END bhv;
