// Logisim project D_Flip_Flop_circ.circ as structural Verilog
module main (
  input  D,
  input  in_2,
  input  in_3,
  input  in_4,
  output Q,
  output out_6
);

  wire d_latch_1_q, not_1_out, not_2_out;

  not not_1 (not_1_out, in_2);
  D_Latch d_latch_1 (.d(D), .en(not_1_out), .q(d_latch_1_q));
  not not_2 (not_2_out, not_1_out);
  D_Flip_Flop d_flip_flop_1 (.clk(in_3), .d(in_4), .q(out_6));
  D_Latch d_latch_2 (.d(d_latch_1_q), .en(not_2_out), .q(Q));
endmodule

// VHDL entity D_Flip_Flop, as the project stores it:
--------------------------------------------------------------------------------
-- Project :
-- File    :
-- Autor   :
-- Date    :
--
--------------------------------------------------------------------------------
-- Description :
--
--------------------------------------------------------------------------------

LIBRARY ieee;
USE ieee.std_logic_1164.all;

ENTITY D_Flip_Flop IS
  PORT (

    clk : IN std_logic;
    d   : IN std_logic;
    q   : OUT std_logic

    );
END D_Flip_Flop;

--------------------------------------------------------------------------------
--Complete your VHDL description below
--------------------------------------------------------------------------------

ARCHITECTURE bhv OF D_Flip_Flop IS

BEGIN
    process(clk)
    begin
        if rising_edge(clk) then
            q <= d;
        end if;
    end process;

END bhv;

// VHDL entity D_Latch, as the project stores it:
--------------------------------------------------------------------------------
-- Project :
-- File    :
-- Autor   :
-- Date    :
--
--------------------------------------------------------------------------------
-- Description :
--
--------------------------------------------------------------------------------

LIBRARY ieee;
USE ieee.std_logic_1164.all;

ENTITY D_Latch IS
  PORT (
	d  : IN std_logic;
	en : IN std_logic;
	q  : OUT std_logic
	);
END D_Latch;

--------------------------------------------------------------------------------
--Complete your VHDL description below
--------------------------------------------------------------------------------

ARCHITECTURE bhv OF D_Latch IS

BEGIN
	
process(d, en)
	begin
		if en = '1' then
			q <= d;
		end if;
	end process;

END bhv;
