// Logisim project D_Latch_circ.circ as structural Verilog
module main (
  input  D,
  input  CLK,
  input  in_3,
  input  in_4,
  output Q,
  output NQ,
  output out_7
);

  wire nand_1_out, nand_2_out, not_1_out;

  not not_1 (not_1_out, D);
  nand nand_1 (nand_1_out, D, CLK);
  nand nand_2 (nand_2_out, CLK, not_1_out);
  nand nand_3 (Q, nand_1_out, NQ);
  nand nand_4 (NQ, Q, nand_2_out);
  D_Latch d_latch_1 (.d(in_3), .en(in_4), .q(out_7));
endmodule

// VHDL entity D_Latch, as the project stores it:
--------------------------------------------------------------------------------
-- Project :
-- File    :
-- Autor   :
-- Date    :
--
--------------------------------------------------------------------------------
-- Description :
--
--------------------------------------------------------------------------------

LIBRARY ieee;
USE ieee.std_logic_1164.all;

ENTITY D_Latch IS
  PORT (
	d  : IN std_logic;
	en : IN std_logic;
	q  : OUT std_logic
	);
END D_Latch;

--------------------------------------------------------------------------------
--Complete your VHDL description below
--------------------------------------------------------------------------------

ARCHITECTURE bhv OF D_Latch IS

BEGIN
	process(d, en)
	begin
		if en = '1' then
			q <= d;
		end if;
	end process;

END bhv;
