// Logisim project JK_Flip_Flop_circ.circ as structural Verilog
module main (
  input  J,
  input  CLK,
  input  K,
  input  in_4,
  input  in_5,
  input  in_6,
  output Q,
  output out_8,
  output out_9
);

  wire nand_1_out, nand_2_out;

  nand nand_1 (nand_1_out, out_8, J, CLK);
  nand nand_2 (nand_2_out, CLK, K, Q);
  nand nand_3 (Q, nand_1_out, out_8);
  nand nand_4 (out_8, Q, nand_2_out);
  JK_Flip_Flop jk_flip_flop_1 (.clk(in_4), .j(in_5), .k(in_6), .q(out_9));
endmodule

// VHDL entity JK_Flip_Flop, as the project stores it:
--------------------------------------------------------------------------------
-- Project :
-- File    :
-- Autor   :
-- Date    :
--
--------------------------------------------------------------------------------
-- Description :
--
--------------------------------------------------------------------------------

LIBRARY ieee;
USE ieee.std_logic_1164.all;

ENTITY JK_Flip_Flop IS
  PORT (
    	   clk : IN std_logic;
        j   : IN std_logic;
        k   : IN std_logic;
        q   : OUT std_logic

    );
END JK_Flip_Flop;

--------------------------------------------------------------------------------
--Complete your VHDL description below
--------------------------------------------------------------------------------

ARCHITECTURE bhv OF JK_Flip_Flop IS
	signal q_int : std_logic := '0';
BEGIN
    process(clk)
    begin
        if rising_edge(clk) then
            if j = '0' and k = '0' then
                q_int <= q_int;

            elsif j = '0' and k = '1' then
                q_int <= '0';

            elsif j = '1' and k = '0' then
                q_int <= '1';

            elsif j = '1' and k = '1' then
                q_int <= not q_int;
            end if;
        end if;
    end process;

    q <= q_int;

END bhv;
