// Logisim project RS_Latch_circ.circ as structural Verilog
module main (
  input  NS,
  input  NR,
  input  in_3,
  input  in_4,
  output out_5,
  output out_6,
  output out_7
);

  nor nor_1 (out_5, NS, out_6);
  nor nor_2 (out_6, out_5, NR);
  RS_Latch rs_latch_1 (.s(in_3), .r(in_4), .q(out_7));
endmodule

// VHDL entity RS_Latch, as the project stores it:
--------------------------------------------------------------------------------
-- Project :
-- File    :
-- Autor   :
-- Date    :
--
--------------------------------------------------------------------------------
-- Description :
--
--------------------------------------------------------------------------------

LIBRARY ieee;
USE ieee.std_logic_1164.all;

ENTITY RS_Latch IS
  PORT (
  		s : IN std_logic;
		r : IN std_logic;
		q : OUT std_logic
	);
END RS_Latch;

--------------------------------------------------------------------------------
--Complete your VHDL description below
--------------------------------------------------------------------------------

ARCHITECTURE bhv OF RS_Latch IS

BEGIN
process(s, r)
	begin
		if s = '1' and r = '0' then
			q <= '1';
		elsif s = '0' and r = '1' then
			q <= '0';
		elsif s = '1' and r = '1' then
			q <= 'X';
		end if;
	end process;

END bhv;
