// Logisim project 7week_problem1.circ as structural Verilog
module main (
  input  in_1,
  input  in_2,
  input  in_3,
  input  in_4,
  output out_5,
  output out_6
);

  AND_OR_Gate and_or_gate_1 (.a(in_1), .b(in_2), .c(in_3), .d(in_4), .out1(out_5), .out2(out_6));
endmodule

// VHDL entity AND_OR_Gate, as the project stores it:
LIBRARY ieee;
USE ieee.std_logic_1164.all;
USE ieee.std_logic_arith.all;
USE ieee.std_logic_unsigned.all;

ENTITY AND_OR_Gate IS
  PORT (
  ------------------------------------------------------------------------------
  --Insert input ports below
    a,b,c,d    : IN  std_logic;
  ------------------------------------------------------------------------------
  --Insert output ports below
    out1, out2 : OUT std_logic
    );
END AND_OR_Gate;

--------------------------------------------------------------------------------
--Complete your VHDL description below
--------------------------------------------------------------------------------

ARCHITECTURE bhv OF AND_OR_Gate IS

BEGIN
	out1 <= a and b and c and d;
	out2 <= a or b or c or d;


END ARCHITECTURE bhv;
