// Logisim project 7week_problem3.circ as structural Verilog
module main (
  input  in_1,
  input  [2:0] in_2
);

  wire a, b, c, d, dp, e, f, g;

  _7_Segment_Display u_7_segment_display_1 (.g(g), .f(f), .a(a), .b(b), .e(e), .d(d), .c(c), .dp(dp));
  led led_1 (.en(in_1), .dat(in_2), .display({a, b, c, d, e, f, g, dp}));
endmodule

// VHDL entity led, as the project stores it:
LIBRARY ieee;
USE ieee.std_logic_1164.all;
USE ieee.std_logic_arith.all;
USE ieee.std_logic_unsigned.all;



ENTITY led IS
  PORT (
  ------------------------------------------------------------------------------
  --Insert input ports below
    en         : IN  std_logic;
    dat        : IN  std_logic_vector(2 DOWNTO 0);

    display    : OUT std_logic_vector(7 downto 0)
    );
END led;

--------------------------------------------------------------------------------
--Complete your VHDL description below
--------------------------------------------------------------------------------

ARCHITECTURE bhv OF led IS

BEGIN
	process(en,dat)
	begin
		if en='0' then
			display <= "ZZZZZZZZ";
		else
			case dat is
				when "000" => display <= "11111011";
				when "001" => display <= "00111111";
				when "010" => display <= "00011011";
				when "011" => display <= "01111011";
				when "100" => display <= "10001111";
				when "101" => display <= "11110111";
				when others => display <= "00000000";
			end case;
		end if;
	end process;

END bhv;
